# Fritzing sketch chickendoor-fritzing (saved by Fritzing 0.9.4)
circuit board: 10.7cm x 7.7cm
breadboards: 1

parts:
  U1 = ESP32-38PinWide [part_number=ESP32-38PinWide]
  J1 = Screw terminal - 2 pins [package=THT]

nets:
  N1: U1.GND, J1.pin1

custom parts:
  ESP32-38PinWide: Generic 38-Pin ESP32 with wide format (only access to one side of pins on a breadboard) based on Stephen Lilley's HiLetgo ESP-WROOM-32 ESP32 ESP-32S Development Board.
